// Logisim project CPU.circ as structural Verilog
module main (
  input  [11:0] Instrucao_IDEC,
  input  [7:0] Entrada_DM,
  output R0_REG,
  output [7:0] Data_DM
);

  wire clk, rwctl;
  wire [7:0] Adress, DM_Out;
  wire [11:0] Out_IM;

  Clock clock_1 (.out(clk));
  RAM #(.bus("separate")) ram_1 (
    .addr(Adress), .din(Entrada_DM), .data(DM_Out), .str(rwctl), .sel(1'b1), .clk(clk), .ld(1'b1));  // open: clr
  CPU cpu_1 ();
  ROM #(.dataWidth(12)) rom_1 (.addr(Data_DM), .data(Out_IM), .sel(rwctl));

  // Other names for the same wires on the sheet: PC_Out[7:0] = Data_DM

  // Notes on the sheet:
  //   RAM - Data Memory
  //   ROM - Instruction Memory
  //   contents of rom_1 (hex, n*v repeats v):
  //   b00 c00 d10 b0a d20 b01 d30 812 200 e0e 331 d10 b01 e07 d01 c00 f00
endmodule

// REG
module Registrador (
  input  [3:0] RsX,
  input  [3:0] RsY,
  input  [3:0] Rd,
  input  [7:0] Rin,
  input  rwctl,
  output R0,
  output [7:0] Rx,
  output [7:0] Ry
);

  wire comparator_1_eq, demultiplexer_1_out0, demultiplexer_1_out1, demultiplexer_1_out2,
       demultiplexer_1_out3, demultiplexer_1_out4, demultiplexer_1_out5, demultiplexer_1_out6,
       demultiplexer_1_out7, demultiplexer_1_out8, demultiplexer_1_out9, demultiplexer_1_out10,
       demultiplexer_1_out11, demultiplexer_1_out12, demultiplexer_1_out13, demultiplexer_1_out14,
       demultiplexer_1_out15, undriven;
  wire [7:0] register_1_q, register_2_q, register_3_q, register_4_q, register_5_q, register_6_q,
       register_7_q, register_8_q, register_9_q, register_10_q, register_11_q, register_12_q, register_13_q,
       register_14_q, register_15_q, register_16_q;

  // NOT_Gate not_1 is placed but not wired
  Demultiplexer #(.select(4), .enable("false")) demultiplexer_1 (
    .out0(demultiplexer_1_out0), .out1(demultiplexer_1_out1), .out2(demultiplexer_1_out2),
    .out3(demultiplexer_1_out3), .out4(demultiplexer_1_out4), .out5(demultiplexer_1_out5),
    .out6(demultiplexer_1_out6), .out7(demultiplexer_1_out7), .out8(demultiplexer_1_out8),
    .out9(demultiplexer_1_out9), .out10(demultiplexer_1_out10), .out11(demultiplexer_1_out11),
    .out12(demultiplexer_1_out12), .out13(demultiplexer_1_out13), .out14(demultiplexer_1_out14),
    .out15(demultiplexer_1_out15), .in(rwctl), .sel(Rd));
  not not_2 (R0, comparator_1_eq);
  Comparator comparator_1 (.a({8{1'b0}}), .b(Rin), .eq(comparator_1_eq));  // open: gt, lt
  Register register_1 (.D(Rin), .Q(register_1_q), .clk(demultiplexer_1_out0));  // open: en, clr
  Register register_2 (.D(Rin), .Q(register_2_q), .clk(demultiplexer_1_out1));  // open: en, clr
  Register register_3 (.D(Rin), .Q(register_3_q), .clk(demultiplexer_1_out2));  // open: en, clr
  Register register_4 (.D(Rin), .Q(register_4_q), .clk(demultiplexer_1_out3));  // open: en, clr
  Register register_5 (.D(Rin), .Q(register_5_q), .clk(demultiplexer_1_out4));  // open: en, clr
  Register register_6 (.D(Rin), .Q(register_6_q), .clk(demultiplexer_1_out5));  // open: en, clr
  Register register_7 (.D(Rin), .Q(register_7_q), .clk(demultiplexer_1_out6));  // open: en, clr
  Register register_8 (.D(Rin), .Q(register_8_q), .clk(demultiplexer_1_out7));  // open: en, clr
  Register register_9 (.D(Rin), .en(undriven), .Q(register_9_q), .clk(demultiplexer_1_out8));  // open: clr
  Register register_10 (.D(Rin), .Q(register_10_q), .clk(demultiplexer_1_out9));  // open: en, clr
  Register register_11 (.D(Rin), .Q(register_11_q), .clk(demultiplexer_1_out10));  // open: en, clr
  Register register_12 (.D(Rin), .Q(register_12_q), .clk(demultiplexer_1_out11));  // open: en, clr
  Register register_13 (.D(Rin), .Q(register_13_q), .clk(demultiplexer_1_out12));  // open: en, clr
  Register register_14 (.D(Rin), .Q(register_14_q), .clk(demultiplexer_1_out13));  // open: en, clr
  Register register_15 (.D(Rin), .Q(register_15_q), .clk(demultiplexer_1_out14));  // open: en, clr
  Register register_16 (.D(Rin), .Q(register_16_q), .clk(demultiplexer_1_out15));  // open: en, clr
  Multiplexer #(.select(4), .width(8), .enable("false")) multiplexer_1 (
    .in0(register_1_q), .in1(register_2_q), .in2(register_3_q), .in3(register_4_q), .in4(register_5_q),
    .in5(register_6_q), .in6(register_7_q), .in7(register_8_q), .in8(register_9_q), .in9(register_10_q),
    .in10(register_11_q), .in11(register_12_q), .in12(register_13_q), .in13(register_14_q),
    .in14(register_15_q), .in15(register_16_q), .out(Rx), .sel(RsX));
  Multiplexer #(.select(4), .width(8), .enable("false")) multiplexer_2 (
    .in0(register_1_q), .in1(register_2_q), .in2(register_3_q), .in3(register_4_q), .in4(register_5_q),
    .in5(register_6_q), .in6(register_7_q), .in7(register_8_q), .in8(register_9_q), .in9(register_10_q),
    .in10(register_11_q), .in11(register_12_q), .in12(register_13_q), .in13(register_14_q),
    .in14(register_15_q), .in15(register_16_q), .out(Ry), .sel(RsY));

  // Other names for the same wires on the sheet: Rs1[3:0] = RsX; Rs2[3:0] = RsY
endmodule

// ULA
module \Unidade_Lógica_Aritimética  (
  input  [7:0] Ix,
  input  [7:0] Iy,
  input  [3:0] Op,
  output [7:0] Out
);

  wire comparator_1_eq, comparator_2_eq, comparator_3_lt, comparator_4_eq, comparator_4_lt, or_2_out;
  wire [7:0] adder_1_out, and_1_out, bit_extender_1_out, bit_extender_2_out, bit_extender_3_out,
       bit_extender_4_out, divider_1_out, multiplier_1_out, or_1_out, subtractor_1_out;

  assign and_1_out = Ix & Iy;  // AND_Gate and_1, 8 bits wide
  assign or_1_out = Ix | Iy;  // OR_Gate or_1, 8 bits wide
  Comparator comparator_1 (.a({8{1'b0}}), .b(Iy), .eq(comparator_1_eq));  // open: gt, lt
  Adder adder_1 (.a(Ix), .b(Iy), .out(adder_1_out));  // open: cin, cout
  Subtractor subtractor_1 (.a(Ix), .b(Iy), .out(subtractor_1_out));  // open: bin, bout
  Multiplier multiplier_1 (.a(Ix), .b(Iy), .out(multiplier_1_out));  // open: cin, cout
  Divider divider_1 (.a(Ix), .b(Iy), .out(divider_1_out));  // open: upper, rem
  Comparator comparator_2 (.a(Ix), .b(Iy), .eq(comparator_2_eq));  // open: gt, lt
  Comparator comparator_3 (.a(Ix), .b(Iy), .lt(comparator_3_lt));  // open: gt, eq
  Comparator comparator_4 (.a(Ix), .b(Iy), .eq(comparator_4_eq), .lt(comparator_4_lt));  // open: gt
  assign bit_extender_1_out = {{7{1'b0}}, comparator_1_eq};  // Bit_Extender bit_extender_1
  or or_2 (or_2_out, comparator_4_eq, comparator_4_lt);
  assign bit_extender_2_out = {{7{1'b0}}, comparator_2_eq};  // Bit_Extender bit_extender_2
  assign bit_extender_3_out = {{7{1'b0}}, comparator_3_lt};  // Bit_Extender bit_extender_3
  assign bit_extender_4_out = {{7{1'b0}}, or_2_out};  // Bit_Extender bit_extender_4
  Multiplexer #(.select(4), .width(8), .enable("false")) multiplexer_1 (
    .in0(and_1_out), .in1(or_1_out), .in2(bit_extender_1_out), .in3(adder_1_out), .in4(subtractor_1_out),
    .in5(multiplier_1_out), .in6(divider_1_out), .in7(bit_extender_2_out), .in8(bit_extender_3_out),
    .in9(bit_extender_4_out), .out(Out), .sel(Op));  // open: in10, in11, in12, in13, in14, in15
endmodule

module REG_ULA (
  input  [3:0] RsX,
  input  [3:0] RsY,
  input  [7:0] \Valor_da_memória ,
  input  [3:0] Rd,
  input  rwctl,
  input  [3:0] Op_ULA,
  input  [2:0] rinctl,
  output [7:0] Out_ULA,
  output R0,
  output [7:0] Rx,
  output [7:0] Ry
);

  wire [7:0] IR, OUT_rinctl, PC, registrador_1_rx, registrador_1_ry;

  Registrador registrador_1 (
    .RsX(RsX), .RsY(RsY), .Rd(Rd), .Rin(OUT_rinctl), .rwctl(rwctl), .R0(R0), .Rx(registrador_1_rx),
    .Ry(registrador_1_ry));
  \Unidade_Lógica_Aritimética  \unidade_lógica_aritimética_1  (
    .Ix(registrador_1_rx), .Iy(registrador_1_ry), .Op(Op_ULA), .Out(Out_ULA));
  Multiplexer #(.select(3), .width(8), .enable("false")) multiplexer_1 (
    .in0(Out_ULA), .in1(\Valor_da_memória ), .in2(IR), .in3(OUT_rinctl), .in4(PC), .out(OUT_rinctl),
    .sel(rinctl));  // open: in5, in6, in7

  // Other names for the same wires on the sheet: Memória[7:0] = \Valor_da_memória ; Op[3:0] = Op_ULA;
  //   Rin[7:0] = OUT_rinctl
endmodule

module IDEC (
  input  [11:0] \INSTRUÇÃO ,
  output [3:0] Op
);


  assign Op = \INSTRUÇÃO [11:8];
endmodule

module CTLU (
  input  [3:0] Op,
  input  R0,
  output rmctl,
  output rwctl,
  output [2:0] rinctl,
  output [1:0] rdctl,
  output wmctl,
  output [1:0] pcctl
);

  wire and_2_out;

  Multiplexer #(.select(4), .enable("false")) multiplexer_1 (
    .in0(1'b0), .in1(1'b0), .in2(1'b0), .in3(1'b0), .in4(1'b0), .in5(1'b0), .in6(1'b0), .in7(1'b0),
    .in8(1'b0), .in9(1'b0), .in10(1'b0), .in11(1'b0), .in12(1'b1), .in13(1'b0), .in14(1'b0), .in15(1'b0),
    .out(rwctl), .sel(Op));
  Multiplexer #(.select(4), .width(3), .enable("false")) multiplexer_2 (
    .in0(3'b000), .in1(3'b000), .in2(3'b000), .in3(3'b000), .in4(3'b000), .in5(3'b000), .in6(3'b000),
    .in7(3'b000), .in8(3'b000), .in9(3'b000), .in10(3'b001), .in11(3'b010), .in12(3'b000), .in13(3'b011),
    .in14(3'b100), .in15(3'b111), .out(rinctl), .sel(Op));
  and and_1 (pcctl[1], Op[3], Op[2], Op[1], ~Op[0], R0);  // AND_Gate
  and and_2 (and_2_out, ~Op[0], ~R0);  // AND_Gate
  Multiplexer #(.select(4), .width(2), .enable("false")) multiplexer_3 (
    .in0(2'b00), .in1(2'b00), .in2(2'b00), .in3(2'b00), .in4(2'b00), .in5(2'b00), .in6(2'b00), .in7(2'b00),
    .in8(2'b00), .in9(2'b00), .in10(2'b00), .in11(2'b00), .in12(2'b10), .in13(2'b10), .in14(2'b01),
    .in15(2'b01), .out(rdctl), .sel(Op));
  or or_1 (pcctl[0], and_2_out, ~Op[3], ~Op[2], ~Op[1]);  // OR_Gate
  Multiplexer #(.select(4), .enable("false")) multiplexer_4 (
    .in0(1'b0), .in1(1'b0), .in2(1'b0), .in3(1'b0), .in4(1'b0), .in5(1'b0), .in6(1'b0), .in7(1'b0),
    .in8(1'b0), .in9(1'b0), .in10(1'b1), .in11(1'b0), .in12(1'b1), .in13(1'b0), .in14(1'b0), .in15(1'b0),
    .out(rmctl), .sel(Op));

  assign wmctl = rmctl;
endmodule

module Memorias (
  input  [7:0] Out_PC,
  input  [7:0] Entrada_DM,
  input  [7:0] Adress_DM,
  output [11:0] Out_IM__Vai_para_IR,
  output [7:0] Data_DM
);

  wire clock_1_out, rwctl;

  Clock clock_1 (.out(clock_1_out));
  ROM #(.dataWidth(12)) rom_1 (.addr(Out_PC), .data(Out_IM__Vai_para_IR), .sel(rwctl));
  RAM #(.bus("separate")) ram_1 (
    .addr(Entrada_DM), .din(Adress_DM), .data(Data_DM), .str(rwctl), .sel(1'b1), .clk(clock_1_out), .ld(1'b1));  // open: clr

  // Other names for the same wires on the sheet: DM_Out[7:0] = Data_DM

  // Notes on the sheet:
  //   ROM - Instruction Memory
  //   RAM - Data Memory
endmodule

module PC (
  input  [7:0] PC_Adress,
  input  [1:0] pcctl,
  input  PC_clk,
  output [7:0] PC_Out
);

  Counter #(.trigger("falling")) counter_1 (
    .load(pcctl[1]), .D(PC_Adress), .count(pcctl[0]), .Q(PC_Out), .clk(PC_clk));  // open: carry, clr
endmodule

module teste (
  input  [3:0] RsX,
  input  [3:0] RsY,
  input  [7:0] \Valor_da_memória ,
  input  [3:0] Rd,
  input  [3:0] Op_ULA,
  output rmctl,
  output wmctl,
  output [1:0] pcctl,
  output [7:0] Adress,
  output [7:0] Out_ULA,
  output [7:0] Rx,
  output [7:0] Ry,
  output [11:0] Out_IM__Vai_para_IR
);

  wire clock_1_out, clock_2_out, R0, rwctl;
  wire [1:0] pcctl_t, rdctl;
  wire [2:0] rinctl;
  wire [3:0] idec_1_op, multiplexer_1_out;
  wire [7:0] IR, multiplexer_2_out, OUT_rinctl, PC, pc_1_pc_out, registrador_1_rx, registrador_1_ry;
  wire [11:8] IR_Out;

  Multiplexer #(.select(2), .width(4), .enable("false")) multiplexer_1 (
    .out(multiplexer_1_out), .sel(rdctl));  // open: in0, in1, in2, in3
  Multiplexer #(.select(3), .width(8), .enable("false")) multiplexer_2 (
    .in0(Out_ULA), .in1(\Valor_da_memória ), .in2(IR), .in3(OUT_rinctl), .in4(PC), .out(multiplexer_2_out),
    .sel(rinctl));  // open: in5, in6, in7
  IDEC idec_1 (.\INSTRUÇÃO ({IR_Out, Adress}), .Op(idec_1_op));
  CTLU ctlu_1 (
    .Op(idec_1_op), .R0(R0), .rmctl(rmctl), .rwctl(rwctl), .rinctl(rinctl), .rdctl(rdctl), .wmctl(wmctl),
    .pcctl(pcctl));
  Registrador registrador_1 (
    .RsX(Adress[7:4]), .RsY(Adress[3:0]), .Rd(multiplexer_1_out), .Rin(multiplexer_2_out), .rwctl(rwctl),
    .R0(R0), .Rx(registrador_1_rx), .Ry(registrador_1_ry));
  \Unidade_Lógica_Aritimética  \unidade_lógica_aritimética_1  (
    .Ix(registrador_1_rx), .Iy(registrador_1_ry), .Op(IR_Out), .Out(Out_ULA));
  PC pc_1 (.PC_Adress(Adress), .pcctl(pcctl_t), .PC_clk(clock_1_out), .PC_Out(pc_1_pc_out));
  Clock clock_1 (.out(clock_1_out));
  Clock clock_2 (.out(clock_2_out));
  IR ir_1 (.IR_In(Out_IM__Vai_para_IR), .rwctl(rwctl), .IR_clk(clock_2_out), .IR_Out({IR_Out, Adress}));
  ROM #(.dataWidth(12)) rom_1 (.addr(pc_1_pc_out), .data(Out_IM__Vai_para_IR), .sel(rwctl));

  // Other names for the same wires on the sheet: IR_Out[7:0] = Adress; RsY_t[3:0] = Adress[3:0];
  //   RsX_t[3:0] = Adress[7:4]; Op[3:0] = IR_Out; Memória[7:0] = \Valor_da_memória 

  // Notes on the sheet:
  //   ROM - Instruction Memory
endmodule

module IR (
  input  [11:0] IR_In,
  input  rwctl,
  input  IR_clk,
  output [11:0] IR_Out
);

  Register #(.width(12)) IR (.D(IR_In), .en(rwctl), .Q(IR_Out), .clk(IR_clk));  // open: clr
endmodule

module CPU___Fixo (
  input  [3:0] RsX,
  input  [7:0] Ix,
  input  [3:0] RsY,
  input  [7:0] Iy,
  input  [3:0] Rd,
  input  [11:0] \Instrução ,
  input  [7:0] Dados_Contador_PC,
  input  clk,
  output R0,
  output [7:0] Out_ULA,
  output [7:0] Rx,
  output [7:0] Ry,
  output [7:0] PC_Out__vai_no_IM,
  output [3:0] out_14,
  output [3:0] out_15,
  output [11:0] IR_Out,
  output [3:0] out_17
);

  wire rmctl_rwctl, rwctl;
  wire [1:0] pcctl, rdctl;
  wire [2:0] rinctl;
  wire [7:0] DM_Out, OUT_rinctl;
  wire [11:0] Out_IM;

  IDEC idec_1 (.\INSTRUÇÃO (\Instrução ), .Op(out_14));
  // CTLU ctlu_1: pin names not known; wires that end beside it: out_14, R0, rwctl, rinctl, rdctl, rmctl_rwctl, pcctl
  Multiplexer #(.select(3), .width(8), .enable("false")) multiplexer_1 (
    .in0(Out_ULA), .in1(DM_Out), .in2(IR_Out[7:0]), .in3(OUT_rinctl), .in4(PC_Out__vai_no_IM),
    .out(OUT_rinctl), .sel(rinctl));  // open: in5, in6, in7
  Registrador registrador_1 (
    .RsX(out_15), .RsY(out_17), .Rd(Rd), .Rin(OUT_rinctl), .rwctl(rwctl), .R0(R0), .Rx(Rx), .Ry(Ry));
  PC pc_1 (.PC_Adress(Dados_Contador_PC), .pcctl(pcctl), .PC_clk(clk), .PC_Out(PC_Out__vai_no_IM));
  IR ir_1 (.IR_In(Out_IM), .rwctl(rwctl), .IR_clk(clk), .IR_Out(IR_Out));
  \Unidade_Lógica_Aritimética  \unidade_lógica_aritimética_1  (.Ix(Ix), .Iy(Iy), .Op(out_14), .Out(Out_ULA));

  // Other names for the same wires on the sheet: Instrucao[11:0] = \Instrução ; IR_Out_REG[7:0] = IR_Out[7:0];
  //   Meio[3:0] = out_15; Menor[3:0] = out_17; Op[3:0] = out_14; PC_Out[7:0] = PC_Out__vai_no_IM

  // Notes on the sheet:
  //   ENTRADAS E SAÍDAS SEPARADAS ULA
  //   ENTRADAS E SAÍDAS SEPARADAS IDEC
  //   ENTRADAS E SAÍDAS SEPARADAS REG
  //   ENTRADAS E SAÍDAS SEPARADAS CPU
endmodule
